# Fritzing sketch wellcom_board (saved by Fritzing 0.9.3b)
circuit board: 16.7535cm x 14.4119cm

parts:
  Arduino_UNO = Arduino Uno (Rev3)  # not connected
  U1 = AD22100 - Voltage Output Temperature Sensor with Signal Conditioning [part_number=AD22100]
  Battery(3_7v_1200mAh) = Lithium Ion Polymer Battery 3.7v 1200mAh [part_number=258]
  Fona_800 = FONA 800 Shield
  Part1 = Adafruit USB DC Solar LiPo Charger [part_number="Adafruit #390"]
  C1 = Capacitor Polarized [package=nippon_f80]

nets:
  N1: U1.V+, Fona_800.3V
  N2: U1.Vo, Fona_800.VIN
  GND: U1.GND, Battery(3_7v_1200mAh).negative, Fona_800.GND, Part1.GND, C1.-
  N3: Battery(3_7v_1200mAh).positive, Part1.BATT
  N4: Fona_800.VBAT, Part1.LOAD
  N5: Part1.DCIN, C1.+

notes:
  5v Solar Panel

custom parts:
  Lithium Ion Polymer Battery 3.7v 1200mAh: Lithium ion polymer (also known as 'lipo' or 'lipoly') batteries are thin, light and powerful. The output ranges from 4.2V when completely charged to 3.7V. This battery has a capacity of 1200mAh for a total of about 4.5 Wh. The batteries come pre-attached with a genuine 2-pin JST-PH connector as shown and include the necessary protection circuitry.
  FONA 800 Shield: This shield fits on top of any classic Arduino or compatible, and packs a surprising amount of technology into it's little frame. At the heart is a GSM cellular module (we use the latest SIM800) the size of a postage stamp. Quad-band 850/900/1800/1900MHz - connect onto any global GSM network with any 2G SIM (in the USA, T-Mobile is suggested) Make and receive voice calls using a headset OR an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
  Adafruit USB DC Solar LiPo Charger: Make your projects to go green this summer with our specialized USB/Solar Lithium Ion Polymer Battery charger! This charger is a very unique design, perfect for outdoor projects, or DIY iPod chargers. We've spent over a year testing and tinkering with this charger to come up with a plug and play solution to charging batteries with the sun and we're really pleased with what we ended up with.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
